// Logisim project Bidirecional.circ as structural Verilog: 1 circuit, main circuit main
module main (
  input  R_L,
  input  in_2,
  input  in_3,
  output out_4,
  output out_5,
  output out_6,
  output out_7
);

  wire clock_1_out, multiplexer_1_out, multiplexer_2_out, multiplexer_3_out, multiplexer_4_out;

  Clock clock_1 (.out(clock_1_out));
  Multiplexer #(.enable("false")) multiplexer_1 (.in0(in_3), .in1(out_6), .out(multiplexer_1_out), .sel(R_L));
  D_Flip_Flop d_ff_1 (.clk(clock_1_out), .D(multiplexer_1_out), .Q(out_5));  // open: Qn, preset, en, reset
  Multiplexer #(.enable("false")) multiplexer_2 (.in0(out_5), .in1(out_7), .out(multiplexer_2_out), .sel(R_L));
  D_Flip_Flop d_ff_2 (.clk(clock_1_out), .D(multiplexer_2_out), .Q(out_6));  // open: Qn, preset, en, reset
  Multiplexer #(.enable("false")) multiplexer_3 (.in0(out_6), .in1(out_4), .out(multiplexer_3_out), .sel(R_L));
  D_Flip_Flop d_ff_3 (.clk(clock_1_out), .D(multiplexer_3_out), .Q(out_7));  // open: Qn, preset, en, reset
  Multiplexer #(.enable("false")) multiplexer_4 (.in0(out_7), .in1(in_2), .out(multiplexer_4_out), .sel(R_L));
  D_Flip_Flop d_ff_4 (.clk(clock_1_out), .D(multiplexer_4_out), .Q(out_4));  // open: Qn, preset, en, reset
endmodule
