// Logisim project Contador crescente 4 bits até o numero 9.circ as structural Verilog: 1 circuit, main circuit main
module main (
  input  clock,
  input  Clear,
  output Q3,
  output Q2,
  output Q1,
  output Q0
);

  wire and_1_out, and_2_out, and_3_out, not_1_out, not_2_out, or_1_out;

  J_K_Flip_Flop j_k_ff_1 (
    .J(1'b1), .clk(clock), .K(1'b1), .Q(Q0), .preset(1'b0), .en(1'b1), .reset(or_1_out));  // open: Qn
  or or_1 (or_1_out, Clear, and_1_out);
  and and_1 (and_1_out, not_1_out, Q1, not_2_out, Q3);
  J_K_Flip_Flop j_k_ff_2 (.J(Q0), .clk(clock), .K(Q0), .Q(Q1), .preset(1'b0), .en(1'b1), .reset(or_1_out));  // open: Qn
  not not_1 (not_1_out, Q0);
  and and_2 (and_2_out, Q0, Q1);
  J_K_Flip_Flop j_k_ff_3 (
    .J(and_2_out), .clk(clock), .K(and_2_out), .Q(Q2), .preset(1'b0), .en(1'b1), .reset(or_1_out));  // open: Qn
  not not_2 (not_2_out, Q2);
  and and_3 (and_3_out, and_2_out, Q2);
  J_K_Flip_Flop j_k_ff_4 (
    .J(and_3_out), .clk(clock), .K(and_3_out), .Q(Q3), .preset(1'b0), .en(1'b1), .reset(or_1_out));  // open: Qn
endmodule
