// Logisim project Contador decrescente 4 bits.circ as structural Verilog: 1 circuit, main circuit main
module main (
  input  in_1,
  output out_2,
  output out_3,
  output out_4,
  output out_5
);

  wire and_1_out, and_2_out, j_k_ff_1_qn, j_k_ff_2_qn, j_k_ff_3_qn;

  J_K_Flip_Flop j_k_ff_1 (
    .J(1'b1), .clk(in_1), .K(1'b1), .Q(out_5), .Qn(j_k_ff_1_qn), .preset(1'b0), .en(1'b1), .reset(1'b0));
  J_K_Flip_Flop j_k_ff_2 (
    .J(j_k_ff_1_qn), .clk(in_1), .K(j_k_ff_1_qn), .Q(out_4), .Qn(j_k_ff_2_qn), .preset(1'b0), .en(1'b1),
    .reset(1'b0));
  J_K_Flip_Flop j_k_ff_3 (
    .J(and_1_out), .clk(in_1), .K(and_1_out), .Q(out_3), .Qn(j_k_ff_3_qn), .preset(1'b0), .en(1'b1),
    .reset(1'b0));
  and and_1 (and_1_out, j_k_ff_2_qn, j_k_ff_1_qn);
  and and_2 (and_2_out, j_k_ff_3_qn, and_1_out);
  J_K_Flip_Flop j_k_ff_4 (
    .J(and_2_out), .clk(in_1), .K(and_2_out), .Q(out_2), .preset(1'b0), .en(1'b1), .reset(1'b0));  // open: Qn
endmodule
