// Logisim project Decodificador_7segmentos teste.circ as structural Verilog: 2 circuits, main circuit main
module main (
  input  in_1,
  input  in_2,
  input  in_3,
  input  in_4
);

  wire decodificador_7seg2_1_a_2, decodificador_7seg2_1_b_2, decodificador_7seg2_1_c_2,
       decodificador_7seg2_1_d_2, decodificador_7seg2_1_e, decodificador_7seg2_1_f, decodificador_7seg2_1_g;

  DECODIFICADOR_7SEG2 decodificador_7seg2_1 (
    .A(in_1), .B(in_2), .C(in_3), .D(in_4), .a_2(decodificador_7seg2_1_a_2), .b_2(decodificador_7seg2_1_b_2),
    .c_2(decodificador_7seg2_1_c_2), .d_2(decodificador_7seg2_1_d_2), .e(decodificador_7seg2_1_e),
    .f(decodificador_7seg2_1_f), .g(decodificador_7seg2_1_g));
  _7_Segment_Display u_7_segment_display_1 (
    .g(decodificador_7seg2_1_g), .f(decodificador_7seg2_1_f), .a(decodificador_7seg2_1_a_2),
    .b(decodificador_7seg2_1_b_2), .e(decodificador_7seg2_1_e), .d(decodificador_7seg2_1_d_2),
    .c(decodificador_7seg2_1_c_2));  // open: dp
endmodule

module DECODIFICADOR_7SEG2 (
  input  A,
  input  B,
  input  C,
  input  D,
  output a_2,
  output b_2,
  output c_2,
  output d_2,
  output e,
  output f,
  output g
);

  wire and_1_out, and_2_out, and_3_out, and_4_out, and_5_out, and_6_out, and_7_out, and_8_out, and_9_out,
       and_10_out, and_11_out, and_12_out, and_13_out, and_14_out, and_15_out, and_16_out, and_17_out,
       not_1_out, not_2_out, not_3_out, not_4_out, not_5_out, not_6_out, not_7_out, not_8_out, not_9_out,
       not_10_out, not_11_out, not_12_out, not_13_out, not_14_out, not_15_out, not_16_out, not_17_out,
       not_18_out, not_19_out, not_20_out, not_21_out, or_1_out, or_2_out, or_3_out, or_4_out, or_6_out,
       or_8_out, or_9_out, or_10_out, or_11_out, or_14_out, or_15_out;

  not not_1 (not_1_out, B);
  and and_1 (and_1_out, not_1_out, not_2_out);
  not not_2 (not_2_out, D);
  and and_2 (and_2_out, B, D);
  not not_3 (not_3_out, B);
  not not_4 (not_4_out, C);
  and and_3 (and_3_out, not_4_out, not_5_out);
  not not_5 (not_5_out, D);
  not not_6 (not_6_out, C);
  or or_1 (or_1_out, not_6_out, D);
  not not_7 (not_7_out, B);
  and and_4 (and_4_out, not_7_out, not_8_out);
  not not_8 (not_8_out, D);
  not not_9 (not_9_out, B);
  and and_5 (and_5_out, not_9_out, C);
  not not_10 (not_10_out, D);
  and and_6 (and_6_out, B, not_11_out);
  not not_11 (not_11_out, C);
  not not_12 (not_12_out, B);
  and and_7 (and_7_out, not_12_out, not_13_out);
  not not_13 (not_13_out, D);
  and and_8 (and_8_out, C, not_14_out);
  not not_14 (not_14_out, D);
  not not_15 (not_15_out, C);
  and and_9 (and_9_out, not_15_out, not_16_out);
  not not_16 (not_16_out, D);
  and and_10 (and_10_out, B, not_17_out);
  not not_17 (not_17_out, C);
  and and_11 (and_11_out, B, not_18_out);
  not not_18 (not_18_out, D);
  not not_19 (not_19_out, B);
  and and_12 (and_12_out, not_19_out, C);
  and and_13 (and_13_out, B, not_20_out);
  not not_20 (not_20_out, C);
  and and_14 (and_14_out, B, not_21_out);
  not not_21 (not_21_out, D);
  or or_2 (or_2_out, and_1_out, C);
  or or_3 (or_3_out, and_2_out, A);
  or or_4 (or_4_out, not_3_out, and_3_out);
  and and_15 (and_15_out, C, D);
  or or_5 (c_2, or_1_out, B);
  or or_6 (or_6_out, and_4_out, and_5_out);
  and and_16 (and_16_out, C, not_10_out);
  and and_17 (and_17_out, and_6_out, D);
  or or_7 (e, and_7_out, and_8_out);
  or or_8 (or_8_out, and_9_out, and_10_out);
  or or_9 (or_9_out, and_11_out, A);
  or or_10 (or_10_out, and_12_out, and_13_out);
  or or_11 (or_11_out, and_14_out, A);
  or or_12 (a_2, or_2_out, or_3_out);
  or or_13 (b_2, or_4_out, and_15_out);
  or or_14 (or_14_out, or_6_out, and_16_out);
  or or_15 (or_15_out, and_17_out, A);
  or or_16 (f, or_8_out, or_9_out);
  or or_17 (g, or_10_out, or_11_out);
  or or_18 (d_2, or_14_out, or_15_out);
endmodule
