// Logisim project PISO.circ as structural Verilog: 1 circuit, main circuit main
module main (
  input  D0,
  input  D1,
  input  D2,
  input  D3,
  input  M,
  output out_6
);

  wire and_1_out, and_2_out, and_3_out, and_4_out, and_5_out, and_6_out, and_7_out, clock_1_out, d_ff_1_q,
       d_ff_2_q, d_ff_3_q, not_1_out, or_1_out, or_2_out, or_3_out;

  Clock clock_1 (.out(clock_1_out));
  not not_1 (not_1_out, M);
  and and_1 (and_1_out, D0, not_1_out);
  D_Flip_Flop d_ff_1 (
    .clk(clock_1_out), .D(and_1_out), .Q(d_ff_1_q), .preset(1'b0), .en(1'b1), .reset(1'b0));  // open: Qn
  and and_2 (and_2_out, d_ff_1_q, M);
  and and_3 (and_3_out, not_1_out, D1);
  or or_1 (or_1_out, and_2_out, and_3_out);
  and and_4 (and_4_out, d_ff_2_q, M);
  or or_2 (or_2_out, and_4_out, and_6_out);
  D_Flip_Flop d_ff_2 (
    .clk(clock_1_out), .D(or_1_out), .Q(d_ff_2_q), .preset(1'b0), .en(1'b1), .reset(1'b0));  // open: Qn
  and and_5 (and_5_out, d_ff_3_q, M);
  and and_6 (and_6_out, not_1_out, D2);
  D_Flip_Flop d_ff_3 (
    .clk(clock_1_out), .D(or_2_out), .Q(d_ff_3_q), .preset(1'b0), .en(1'b1), .reset(1'b0));  // open: Qn
  and and_7 (and_7_out, not_1_out, D3);
  or or_3 (or_3_out, and_5_out, and_7_out);
  D_Flip_Flop d_ff_4 (.clk(clock_1_out), .D(or_3_out), .Q(out_6), .preset(1'b0), .en(1'b1), .reset(1'b0));  // open: Qn
endmodule
