// Logisim project Somador_subtrador_8bits.circ as structural Verilog: 1 circuit, main circuit main
module main (
  input  in_1,
  input  in_2,
  input  in_3,
  input  in_4,
  input  in_5,
  input  in_6,
  input  in_7,
  input  in_8,
  input  in_9,
  output out_10,
  output out_11,
  output out_12,
  output out_13,
  output out_14
);

  // Somador_Subtrador_4bits_main main_1: pin names not known; wires that end beside it: out_10, in_4, in_3, in_2, out_14, out_12, in_1, out_13, in_8, out_12, in_7, out_11, in_6, in_9, in_5
endmodule
