// Logisim project Subtrator.circ as structural Verilog: 1 circuit, main circuit main
module main (
  input  A3,
  input  B3,
  input  A2,
  input  B2,
  input  A1,
  input  B1,
  input  A0,
  input  B0,
  output Q_carry,
  output R,
  output R_2,
  output R_3,
  output R_4
);

  wire main_1_vai_um, main_2_vai_um, main_3_vai_um, main_4_vai_um, not_1_out, not_2_out, not_3_out,
       not_4_out, not_5_out, not_6_out, not_7_out, not_8_out, not_10_out, not_11_out, not_12_out;

  not not_1 (not_1_out, B3);
  not not_2 (not_2_out, not_10_out);
  not not_3 (not_3_out, B2);
  not not_4 (not_4_out, not_11_out);
  not not_5 (not_5_out, B1);
  not not_6 (not_6_out, not_12_out);
  not not_7 (not_7_out, B0);
  not not_8 (not_8_out, 1'b0);
  somador_de_1_bit_certo_main main_1 (.A(A3), .B(not_1_out), .Vem_um(not_2_out), .R1(R), .vai_um(main_1_vai_um));
  somador_de_1_bit_certo_main main_2 (.A(A2), .B(not_3_out), .Vem_um(not_4_out), .R1(R_2), .vai_um(main_2_vai_um));
  somador_de_1_bit_certo_main main_3 (.A(A1), .B(not_5_out), .Vem_um(not_6_out), .R1(R_3), .vai_um(main_3_vai_um));
  somador_de_1_bit_certo_main main_4 (.A(A0), .B(not_7_out), .Vem_um(not_8_out), .R1(R_4), .vai_um(main_4_vai_um));
  not not_9 (Q_carry, main_1_vai_um);
  not not_10 (not_10_out, main_2_vai_um);
  not not_11 (not_11_out, main_3_vai_um);
  not not_12 (not_12_out, main_4_vai_um);
endmodule
