// Logisim project blabalbalbalbalbala.circ as structural Verilog: 1 circuit, main circuit main
module main (
  input  A3,
  input  A2,
  input  A1,
  input  A0,
  input  B3,
  input  B2,
  input  B1,
  input  B0,
  input  E,
  output Q,
  output R3,
  output R2,
  output R1,
  output R0
);

  wire main_2_vai_um, main_3_vai_um, main_4_vai_um, xor_1_out, xor_2_out, xor_3_out, xor_4_out;

  xor xor_1 (xor_1_out, B3, E);
  somador_de_1_bit_certo_main main_1 (.A(A3), .B(xor_1_out), .Vem_um(main_2_vai_um), .R1(R3), .vai_um(Q));
  xor xor_2 (xor_2_out, B2, E);
  somador_de_1_bit_certo_main main_2 (.A(A2), .B(xor_2_out), .Vem_um(main_3_vai_um), .R1(R2), .vai_um(main_2_vai_um));
  xor xor_3 (xor_3_out, B1, E);
  somador_de_1_bit_certo_main main_3 (.A(A1), .B(xor_3_out), .Vem_um(main_4_vai_um), .R1(R1), .vai_um(main_3_vai_um));
  xor xor_4 (xor_4_out, B0, E);
  somador_de_1_bit_certo_main main_4 (.A(A0), .B(xor_4_out), .Vem_um(E), .R1(R0), .vai_um(main_4_vai_um));
endmodule
