// Logisim project contador até o numero 9 COM DECODIFICADOR.circ as structural Verilog: 1 circuit, main circuit main
module main (
  input  in_1
);

  wire clock_1_out, decodificador_7seg2_1_a_2, decodificador_7seg2_1_b_2, decodificador_7seg2_1_c_2,
       decodificador_7seg2_1_d_2, decodificador_7seg2_1_e, decodificador_7seg2_1_f, decodificador_7seg2_1_g,
       main_1_q0, main_1_q1, main_1_q2, main_1_q3;

  Clock clock_1 (.out(clock_1_out));
  \Contador_crescente_4_bits_até_o_numero_9_main  main_1 (
    .clock(clock_1_out), .Clear(in_1), .Q3(main_1_q3), .Q2(main_1_q2), .Q1(main_1_q1), .Q0(main_1_q0));
  DECODIFICADOR_7SEG2 decodificador_7seg2_1 (
    .A(main_1_q3), .B(main_1_q2), .C(main_1_q1), .D(main_1_q0), .a_2(decodificador_7seg2_1_a_2),
    .b_2(decodificador_7seg2_1_b_2), .c_2(decodificador_7seg2_1_c_2), .d_2(decodificador_7seg2_1_d_2),
    .e(decodificador_7seg2_1_e), .f(decodificador_7seg2_1_f), .g(decodificador_7seg2_1_g));
  _7_Segment_Display u_7_segment_display_1 (
    .g(decodificador_7seg2_1_g), .f(decodificador_7seg2_1_f), .a(decodificador_7seg2_1_a_2),
    .b(decodificador_7seg2_1_b_2), .e(decodificador_7seg2_1_e), .d(decodificador_7seg2_1_d_2),
    .c(decodificador_7seg2_1_c_2));  // open: dp
endmodule
