// Logisim project contador de 1 minuto .circ as structural Verilog: 1 circuit, main circuit main
module main (
  input  clear
);

  wire and_1_out, clock_out, decodificador_7seg2_1_a_2, decodificador_7seg2_1_b_2, decodificador_7seg2_1_c_2,
       decodificador_7seg2_1_d_2, decodificador_7seg2_1_e, decodificador_7seg2_1_f, decodificador_7seg2_1_g,
       decodificador_7seg2_2_a_2, decodificador_7seg2_2_b_2, decodificador_7seg2_2_c_2,
       decodificador_7seg2_2_d_2, decodificador_7seg2_2_e, decodificador_7seg2_2_f, decodificador_7seg2_2_g,
       main_1_q0, main_1_q1, main_1_q2, main_1_q3, main_2_q0, main_2_q1, main_2_q2, main_2_q3, nor_1_out;

  nor nor_1 (nor_1_out, main_1_q0, main_1_q1, main_1_q2, main_1_q3);
  Clock clock (.out(clock_out));
  \Contador_crescente_4_bits_até_o_numero_9_main  main_1 (
    .clock(clock_out), .Clear(clear), .Q3(main_1_q3), .Q2(main_1_q2), .Q1(main_1_q1), .Q0(main_1_q0));
  and and_1 (and_1_out, main_2_q1, main_2_q2);
  DECODIFICADOR_7SEG2 decodificador_7seg2_1 (
    .A(main_1_q3), .B(main_1_q2), .C(main_1_q1), .D(main_1_q0), .a_2(decodificador_7seg2_1_a_2),
    .b_2(decodificador_7seg2_1_b_2), .c_2(decodificador_7seg2_1_c_2), .d_2(decodificador_7seg2_1_d_2),
    .e(decodificador_7seg2_1_e), .f(decodificador_7seg2_1_f), .g(decodificador_7seg2_1_g));
  \Contador_crescente_4_bits_até_o_numero_9_main  main_2 (
    .clock(nor_1_out), .Clear(and_1_out), .Q3(main_2_q3), .Q2(main_2_q2), .Q1(main_2_q1), .Q0(main_2_q0));
  _7_Segment_Display u_7_segment_display_1 (
    .g(decodificador_7seg2_1_g), .f(decodificador_7seg2_1_f), .a(decodificador_7seg2_1_a_2),
    .b(decodificador_7seg2_1_b_2), .e(decodificador_7seg2_1_e), .d(decodificador_7seg2_1_d_2),
    .c(decodificador_7seg2_1_c_2));  // open: dp
  DECODIFICADOR_7SEG2 decodificador_7seg2_2 (
    .A(main_2_q3), .B(main_2_q2), .C(main_2_q1), .D(main_2_q0), .a_2(decodificador_7seg2_2_a_2),
    .b_2(decodificador_7seg2_2_b_2), .c_2(decodificador_7seg2_2_c_2), .d_2(decodificador_7seg2_2_d_2),
    .e(decodificador_7seg2_2_e), .f(decodificador_7seg2_2_f), .g(decodificador_7seg2_2_g));
  _7_Segment_Display u_7_segment_display_2 (
    .g(decodificador_7seg2_2_g), .f(decodificador_7seg2_2_f), .a(decodificador_7seg2_2_a_2),
    .b(decodificador_7seg2_2_b_2), .e(decodificador_7seg2_2_e), .d(decodificador_7seg2_2_d_2),
    .c(decodificador_7seg2_2_c_2));  // open: dp
endmodule
