// Logisim project somador de 1 bit certo.circ as structural Verilog: 1 circuit, main circuit main
module main (
  input  A,
  input  B,
  input  Vem_um,
  output R1,
  output vai_um
);

  wire and_1_out, and_2_out, xor_1_out;

  _7_Segment_Display u_7_segment_display_1 (.g(1'b1), .a(1'b1), .b(1'b1), .e(1'b1), .d(1'b1));  // open: f, c, dp
  _7_Segment_Display u_7_segment_display_2 (.g(1'b1), .a(1'b1), .b(1'b1), .e(1'b1), .d(1'b1), .dp(1'b1));  // open: f, c
  xor xor_1 (xor_1_out, A, B);
  and and_1 (and_1_out, A, B);
  _7_Segment_Display u_7_segment_display_3 (.f(1'b1), .a(1'b1), .b(1'b1), .e(1'b1), .d(1'b1), .c(1'b1));  // open: g, dp
  _7_Segment_Display u_7_segment_display_4 (.g(1'b1), .f(1'b1), .a(1'b1), .b(1'b1), .d(1'b1), .c(1'b1));  // open: e, dp
  _7_Segment_Display u_7_segment_display_5 (.g(1'b1), .f(1'b1), .a(1'b1), .d(1'b1), .c(1'b1));  // open: b, e, dp
  and and_2 (and_2_out, xor_1_out, Vem_um);
  _7_Segment_Display u_7_segment_display_6 (.g(1'b1), .f(1'b1), .b(1'b1), .c(1'b1));  // open: a, e, d, dp
  xor xor_2 (R1, xor_1_out, Vem_um);
  or or_1 (vai_um, and_2_out, and_1_out);
  _7_Segment_Display u_7_segment_display_7 (.g(1'b1), .f(1'b1), .a(1'b1), .e(1'b1), .d(1'b1), .c(1'b1));  // open: b, dp
endmodule
