// Logisim project teste.circ as structural Verilog: 1 circuit, main circuit main
module main (
  input  A,
  input  A1,
  input  A0,
  input  A1_2,
  input  A0_2,
  input  B,
  input  B1,
  input  B0,
  input  B1_2,
  input  B0_2,
  input  C_in,
  output R,
  output Q,
  output R3,
  output R2,
  output R1,
  output R0,
  output Vai_1
);

  wire and_2_out, and_3_out, and_4_out, and_5_out, and_6_out, and_7_out, and_8_out, and_9_out, or_1_out,
       or_2_out, or_3_out, xor_2_out, xor_3_out, xor_6_out, xor_7_out;

  _7_Segment_Display u_7_segment_display_1 (.g(1'b1), .a(1'b1), .b(1'b1), .e(1'b1), .d(1'b1));  // open: f, c, dp
  xor xor_1 (R, A, B);
  and and_1 (Vai_1, A, B);
  _7_Segment_Display u_7_segment_display_2 (.g(1'b1), .a(1'b1), .b(1'b1), .e(1'b1), .d(1'b1), .dp(1'b1));  // open: f, c
  _7_Segment_Display u_7_segment_display_3 (.f(1'b1), .a(1'b1), .b(1'b1), .e(1'b1), .d(1'b1), .c(1'b1));  // open: g, dp
  _7_Segment_Display u_7_segment_display_4 (.g(1'b1), .f(1'b1), .a(1'b1), .b(1'b1), .d(1'b1), .c(1'b1));  // open: e, dp
  _7_Segment_Display u_7_segment_display_5 (.g(1'b1), .f(1'b1), .a(1'b1), .d(1'b1), .c(1'b1));  // open: b, e, dp
  _7_Segment_Display u_7_segment_display_6 (.g(1'b1), .f(1'b1), .b(1'b1), .c(1'b1));  // open: a, e, d, dp
  and and_2 (and_2_out, A0_2, B0_2);
  and and_3 (and_3_out, A0, B0);
  _7_Segment_Display u_7_segment_display_7 (.g(1'b1), .f(1'b1), .a(1'b1), .e(1'b1), .d(1'b1), .c(1'b1));  // open: b, dp
  xor xor_2 (xor_2_out, A0_2, B0_2);
  xor xor_3 (xor_3_out, A0, B0);
  and and_4 (and_4_out, xor_3_out, or_3_out);
  and and_5 (and_5_out, xor_2_out, C_in);
  xor xor_4 (R0, xor_2_out, C_in);
  or or_1 (or_1_out, and_5_out, and_2_out);
  xor xor_5 (R2, xor_3_out, or_3_out);
  or or_2 (or_2_out, and_4_out, and_3_out);
  and and_6 (and_6_out, A1_2, B1_2);
  and and_7 (and_7_out, A1, B1);
  xor xor_6 (xor_6_out, A1_2, B1_2);
  xor xor_7 (xor_7_out, A1, B1);
  and and_8 (and_8_out, xor_6_out, or_1_out);
  and and_9 (and_9_out, xor_7_out, or_2_out);
  xor xor_8 (R3, xor_7_out, or_2_out);
  xor xor_9 (R1, xor_6_out, or_1_out);
  or or_3 (or_3_out, and_8_out, and_6_out);
  or or_4 (Q, and_9_out, and_7_out);
endmodule
